// Logisim project Calculator.circ as structural Verilog: 1 circuit, main circuit main
module main (
  input  \SOMA___TRUE__SUBTRAÇÃO____FALSE ,
  input  _0,
  input  _1,
  input  _2,
  input  _3,
  input  _4,
  input  _5,
  input  _6,
  input  _7,
  input  _8,
  input  _9,
  input  A,
  input  B,
  input  C,
  input  D,
  input  E,
  input  F,
  input  _0_2,
  input  _1_2,
  input  _2_2,
  input  _3_2,
  input  _4_2,
  input  _5_2,
  input  _6_2,
  input  _7_2,
  input  _8_2,
  input  _9_2,
  input  A_2,
  input  B_2,
  input  C_2,
  input  D_2,
  input  E_2,
  input  F_2,
  input  in_34,
  output \É_NEGATIVO ,
  output [4:0] out_36
);

  wire controlled_buffer_1_out, not_1_out, \subtrator_1_é_negativo ;
  wire [3:0] controlled_buffer_2_out, controlled_buffer_6_out, subtrator_1_saida_binaria;
  wire [4:0] soma_out_33;

  Soma_main soma (
    ._0(_0), ._0_2(_0_2), ._1(_1), ._1_2(_1_2), ._2(_2), ._2_2(_2_2), ._3(_3), ._3_2(_3_2), ._4(_4),
    ._4_2(_4_2), ._5(_5), ._5_2(_5_2), ._6(_6), ._6_2(_6_2), ._7(_7), ._7_2(_7_2), ._8(_8), ._8_2(_8_2),
    ._9(_9), ._9_2(_9_2), .A(A), .A_2(A_2), .B(B), .B_2(B_2), .C(C), .C_2(C_2), .D(D), .D_2(D_2), .E(E),
    .E_2(E_2), .F(F), .F_2(F_2), .out_33(soma_out_33));
  SUBTRATOR subtrator_1 (
    ._0(_0), ._0B(_0_2), ._1(_1), ._1B(_1_2), ._2(_2), ._2B(_2_2), ._3(_3), ._3B(_3_2), ._4(_4), ._4B(_4_2),
    ._5(_5), ._5B(_5_2), ._6(_6), ._6B(_6_2), ._7(_7), ._7B(_7_2), ._8(_8), ._8B(_8_2), ._9(_9), ._9B(_9_2),
    .A(A), .AB(A_2), .B(B), .BB(B_2), .C(C), .CB(C_2), .D(D), .DB(D_2), .E(E), .EB(E_2), .F(F), .FB(F_2),
    .\É_NEGATIVO (\subtrator_1_é_negativo ), .saida_binaria(subtrator_1_saida_binaria));
  _7_Segment_Display u_7_segment_display_1 (.g(controlled_buffer_1_out));  // open: f, a, b, e, d, c, dp
  assign controlled_buffer_1_out = not_1_out ? \subtrator_1_é_negativo  : 1'bz;  // Controlled_Buffer controlled_buffer_1
  assign controlled_buffer_2_out = \SOMA___TRUE__SUBTRAÇÃO____FALSE  ? soma_out_33[3:0] : 4'bz;  // Controlled_Buffer controlled_buffer_2
  assign controlled_buffer_2_out = not_1_out ? subtrator_1_saida_binaria : 4'bz;  // Controlled_Buffer controlled_buffer_3
  not not_1 (not_1_out, \SOMA___TRUE__SUBTRAÇÃO____FALSE );
  assign \É_NEGATIVO  = not_1_out ? \subtrator_1_é_negativo  : 1'bz;  // Controlled_Buffer controlled_buffer_4
  assign out_36 = not_1_out ? {1'b0, subtrator_1_saida_binaria} : 5'bz;  // Controlled_Buffer controlled_buffer_5
  Hex_Digit_Display hex_digit_display_1 (.value(controlled_buffer_6_out));  // open: dp
  assign controlled_buffer_6_out = not_1_out ? 4'b0000 : 4'bz;  // Controlled_Buffer controlled_buffer_6
  assign controlled_buffer_6_out = \SOMA___TRUE__SUBTRAÇÃO____FALSE  ? {{3{in_34}}, soma_out_33[4]} : 4'bz;  // Controlled_Buffer controlled_buffer_7
  Hex_Digit_Display hex_digit_display_2 (.value(controlled_buffer_2_out));  // open: dp
  assign out_36 = \SOMA___TRUE__SUBTRAÇÃO____FALSE  ? soma_out_33 : 5'bz;  // Controlled_Buffer controlled_buffer_8
  // Probe on nothing
endmodule
