// Logisim project CONVERSOR.circ as structural Verilog: 1 circuit, main circuit main
// hexa2bin
module main (
  input  _1,
  input  _2,
  input  _3,
  input  _4,
  input  _5,
  input  _6,
  input  _7,
  input  _8,
  input  _9,
  input  A,
  input  B,
  input  C,
  input  D,
  input  E,
  input  F,
  output [3:0] out_16
);

  or S1 (out_16[3], _8, _9, A, B, C, D, E, F);
  or S2 (out_16[2], _4, _5, _6, _7, C, D, E, F);
  or S3 (out_16[1], _2, _3, _6, _7, A, B, E, F);
  or S4 (out_16[0], _1, _3, _5, _7, _9, B, D, F);
endmodule
