// Logisim project Soma.circ as structural Verilog: 1 circuit, main circuit main
module main (
  input  _0,
  input  _1,
  input  _2,
  input  _3,
  input  _4,
  input  _5,
  input  _6,
  input  _7,
  input  _8,
  input  _9,
  input  A,
  input  B,
  input  C,
  input  D,
  input  E,
  input  F,
  input  in_17,
  input  _0B,
  input  _1B,
  input  _2B,
  input  _3B,
  input  _4B,
  input  _5B,
  input  _6B,
  input  _7B,
  input  _8B,
  input  _9B,
  input  AB,
  input  BB,
  input  CB,
  input  DB,
  input  EB,
  input  FB,
  output [4:0] out_34
);

  wire main_3_vai_1, main_5_vai_1, main_6_vai_1;
  wire [3:0] main_1_out_16, main_2_out_16;

  CONVERSOR_main main_1 (
    ._1(_1), ._2(_2), ._3(_3), ._4(_4), ._5(_5), ._6(_6), ._7(_7), ._8(_8), ._9(_9), .A(A), .B(B), .C(C),
    .D(D), .E(E), .F(F), .out_16(main_1_out_16));
  CONVERSOR_main main_2 (
    ._1(_1B), ._2(_2B), ._3(_3B), ._4(_4B), ._5(_5B), ._6(_6B), ._7(_7B), ._8(_8B), ._9(_9B), .A(AB), .B(BB),
    .C(CB), .D(DB), .E(EB), .F(FB), .out_16(main_2_out_16));
  meiosomador_main main_3 (.A(main_2_out_16[0]), .B(main_1_out_16[0]), .S(out_34[0]), .VAI_1(main_3_vai_1));
  somadorinteiro_main main_4 (
    .VEM_1(main_5_vai_1), .A(main_2_out_16[3]), .B(main_1_out_16[3]), .S(out_34[3]), .vai_1(out_34[4]));
  somadorinteiro_main main_5 (
    .VEM_1(main_6_vai_1), .A(main_1_out_16[2]), .B(main_2_out_16[2]), .S(out_34[2]), .vai_1(main_5_vai_1));
  somadorinteiro_main main_6 (
    .VEM_1(main_3_vai_1), .A(main_1_out_16[1]), .B(main_2_out_16[1]), .S(out_34[1]), .vai_1(main_6_vai_1));
  Hex_Digit_Display hex_digit_display_1 (.value({{3{in_17}}, out_34[4]}));  // open: dp
  Hex_Digit_Display hex_digit_display_2 (.value(out_34[3:0]));  // open: dp
endmodule
