// Logisim project Subtração.circ as structural Verilog: 1 circuit, main circuit main
// Subtração
module main (
  input  _0B,
  input  _1B,
  input  _2B,
  input  _3B,
  input  _4B,
  input  _5B,
  input  _6B,
  input  _7B,
  input  _8B,
  input  _9B,
  input  AB,
  input  BB,
  input  CB,
  input  DB,
  input  EB,
  input  FB,
  input  _0,
  input  _1,
  input  _2,
  input  _3,
  input  _4,
  input  _5,
  input  _6,
  input  _7,
  input  _8,
  input  _9,
  input  A,
  input  B,
  input  C,
  input  D,
  input  E,
  input  F,
  output [3:0] out_33
);

  wire subtrator1_1_1_p1, subtrator1_1_1_p5, subtrator1_1_2_p1, subtrator1_2_1_t;
  wire [3:0] main_1_out_16, main_2_out_16;

  CONVERSOR_main main_1 (
    ._1(_1B), ._2(_2B), ._3(_3B), ._4(_4B), ._5(_5B), ._6(_6B), ._7(_7B), ._8(_8B), ._9(_9B), .A(AB), .B(BB),
    .C(CB), .D(DB), .E(EB), .F(FB), .out_16(main_1_out_16));
  CONVERSOR_main main_2 (
    ._1(_1), ._2(_2), ._3(_3), ._4(_4), ._5(_5), ._6(_6), ._7(_7), ._8(_8), ._9(_9), .A(A), .B(B), .C(C),
    .D(D), .E(E), .F(F), .out_16(main_2_out_16));
  subtrator1_2 subtrator1_2_1 (.A(main_2_out_16[0]), .B(main_1_out_16[0]), .S(out_33[0]), .T(subtrator1_2_1_t));
  // subtrator1_1 subtrator1_1_1: pin names not known; wires that end beside it: subtrator1_1_1_p1, main_1_out_16[3], main_2_out_16[3], out_33[3], subtrator1_1_1_p5
  // subtrator1_1 subtrator1_1_2: pin names not known; wires that end beside it: subtrator1_1_2_p1, main_1_out_16[2], main_2_out_16[2], out_33[2], subtrator1_1_1_p1
  // subtrator1_1 subtrator1_1_3: pin names not known; wires that end beside it: subtrator1_2_1_t, main_1_out_16[1], main_2_out_16[1], out_33[1], subtrator1_1_2_p1
endmodule
