// Logisim project Subtraçãocomcoisinhade2.circ as structural Verilog: 1 circuit, main circuit SUBTRATOR
module SUBTRATOR (
  input  _0,
  input  _1,
  input  _2,
  input  _3,
  input  _4,
  input  _5,
  input  _6,
  input  _7,
  input  _8,
  input  _9,
  input  A,
  input  B,
  input  C,
  input  D,
  input  E,
  input  F,
  input  _0B,
  input  _1B,
  input  _2B,
  input  _3B,
  input  _4B,
  input  _5B,
  input  _6B,
  input  _7B,
  input  _8B,
  input  _9B,
  input  AB,
  input  BB,
  input  CB,
  input  DB,
  input  EB,
  input  FB,
  output \É_NEGATIVO ,
  output [3:0] saida_binaria
);

  wire main_3_vai_1, main_4_vai_1, main_5_vai_1, main_6_vai_1, nor_1_out, or_1_out;
  wire [3:0] coisinha_de_2_1_out_2, coisinha_de_2_2_out_2, main_1_out_16, main_2_out_16, main_4_s;

  CONVERSOR_main main_1 (
    ._1(_1), ._2(_2), ._3(_3), ._4(_4), ._5(_5), ._6(_6), ._7(_7), ._8(_8), ._9(_9), .A(A), .B(B), .C(C),
    .D(D), .E(E), .F(F), .out_16(main_1_out_16));
  CONVERSOR_main main_2 (
    ._1(_1B), ._2(_2B), ._3(_3B), ._4(_4B), ._5(_5B), ._6(_6B), ._7(_7B), ._8(_8B), ._9(_9B), .A(AB), .B(BB),
    .C(CB), .D(DB), .E(EB), .F(FB), .out_16(main_2_out_16));
  coisinha_de_2 coisinha_de_2_1 (.entrada_4_bits(main_2_out_16), .out_2(coisinha_de_2_1_out_2));
  nor nor_1 (nor_1_out, coisinha_de_2_1_out_2[0], coisinha_de_2_1_out_2[1], coisinha_de_2_1_out_2[2], coisinha_de_2_1_out_2[3]);
  somadorinteiro_main main_3 (
    .VEM_1(main_4_vai_1), .A(coisinha_de_2_1_out_2[1]), .B(main_1_out_16[1]), .S(main_4_s[1]),
    .vai_1(main_3_vai_1));
  meiosomador_main main_4 (.A(coisinha_de_2_1_out_2[0]), .B(main_1_out_16[0]), .S(main_4_s[0]), .VAI_1(main_4_vai_1));
  somadorinteiro_main main_5 (
    .VEM_1(main_3_vai_1), .A(main_1_out_16[2]), .B(coisinha_de_2_1_out_2[2]), .S(main_4_s[2]),
    .vai_1(main_5_vai_1));
  somadorinteiro_main main_6 (
    .VEM_1(main_5_vai_1), .A(main_1_out_16[3]), .B(coisinha_de_2_1_out_2[3]), .S(main_4_s[3]),
    .vai_1(main_6_vai_1));
  or or_1 (or_1_out, main_6_vai_1, nor_1_out);
  not not_1 (\É_NEGATIVO , or_1_out);
  coisinha_de_2 coisinha_de_2_2 (.entrada_4_bits(main_4_s), .out_2(coisinha_de_2_2_out_2));
  assign saida_binaria = \É_NEGATIVO  ? coisinha_de_2_2_out_2 : 4'bz;  // Controlled_Buffer controlled_buffer_1
  assign saida_binaria = or_1_out ? main_4_s : 4'bz;  // Controlled_Buffer controlled_buffer_2
endmodule
