// Logisim project comp-de2.circ as structural Verilog: 1 circuit, main circuit coisinha de 2
// comp.2
module coisinha_de_2 (
  input  [3:0] entrada_4_bits,
  output [3:0] out_2
);

  wire main_1_vai_1, main_2_vai_1, main_3_vai_1, not_1_out, not_2_out, not_3_out, not_4_out, not_5_out;

  not not_1 (not_1_out, entrada_4_bits[0]);
  not not_2 (not_2_out, entrada_4_bits[1]);
  not not_3 (not_3_out, entrada_4_bits[2]);
  not not_4 (not_4_out, entrada_4_bits[3]);
  meiosomador_main main_1 (.A(not_1_out), .B(1'b1), .S(out_2[0]), .VAI_1(main_1_vai_1));
  not not_5 (not_5_out, 1'b1);
  somadorinteiro_main main_2 (.VEM_1(main_1_vai_1), .A(not_2_out), .B(not_5_out), .S(out_2[1]), .vai_1(main_2_vai_1));
  somadorinteiro_main main_3 (.VEM_1(main_2_vai_1), .A(not_3_out), .B(not_5_out), .S(out_2[2]), .vai_1(main_3_vai_1));
  somadorinteiro_main main_4 (.VEM_1(main_3_vai_1), .A(not_4_out), .B(not_5_out), .S(out_2[3]));  // open: vai_1
endmodule
