// Logisim project meiosomador.circ as structural Verilog: 1 circuit, main circuit main
// Somador 1/2
module main (
  input  A,
  input  B,
  output S,
  output VAI_1
);

  xor xor_1 (S, B, A);
  and and_1 (VAI_1, B, A);
endmodule
