// Logisim project meiosubtrator.circ as structural Verilog: 1 circuit, main circuit subtrator1/2
module subtrator1_2 (
  input  A,
  input  B,
  output S,
  output T
);

  xor xor_1 (S, B, A);
  and and_1 (T, ~A, B);  // AND_Gate
endmodule
