// Logisim project somadorinteiro.circ as structural Verilog: 1 circuit, main circuit main
// somador 1/1
module main (
  input  VEM_1,
  input  A,
  input  B,
  output S,
  output vai_1
);

  wire and_1_out, and_2_out, xor_1_out, xor_2_out;

  xor xor_1 (xor_1_out, B, A);
  and and_1 (and_1_out, A, B);
  xor xor_2 (xor_2_out, B, A);
  xor xor_3 (S, xor_1_out, VEM_1);
  and and_2 (and_2_out, VEM_1, xor_2_out);
  or or_1 (vai_1, and_1_out, and_2_out);
endmodule
