// Logisim project subtratorcompleto.circ as structural Verilog: 1 circuit, main circuit subtrator1/1
module subtrator1_1 (
  input  A,
  input  B,
  input  T,
  output S,
  output Ts
);

  wire and_1_out, and_2_out, xnor_1_out, xor_1_out;

  xnor xnor_1 (xnor_1_out, A, B);
  xor xor_1 (xor_1_out, B, T);
  and and_1 (and_1_out, ~A, B);  // AND_Gate
  and and_2 (and_2_out, T, xnor_1_out);
  xor xor_2 (S, xor_1_out, A);
  or or_1 (Ts, and_1_out, and_2_out);
endmodule
