// Logisim project Soma.circ as structural Verilog: 1 circuit, main circuit main
module main (
  input  _0,
  input  _1,
  input  _2,
  input  _3,
  input  _4,
  input  _5,
  input  _6,
  input  _7,
  input  _8,
  input  _9,
  input  A,
  input  B,
  input  C,
  input  D,
  input  E,
  input  F,
  input  in_17,
  input  _0_2,
  input  _1_2,
  input  _2_2,
  input  _3_2,
  input  _4_2,
  input  _5_2,
  input  _6_2,
  input  _7_2,
  input  _8_2,
  input  _9_2,
  input  A_2,
  input  B_2,
  input  C_2,
  input  D_2,
  input  E_2,
  input  F_2
);

  wire main_3_vai_1, main_5_vai_1, main_6_vai_1;
  wire [0:0] main_4_vai_1;
  wire [3:0] main_1_out_16, main_2_out_16, main_3_s;

  CONVERSOR_main main_1 (
    ._1(_1), ._2(_2), ._3(_3), ._4(_4), ._5(_5), ._6(_6), ._7(_7), ._8(_8), ._9(_9), .A(A), .B(B), .C(C),
    .D(D), .E(E), .F(F), .out_16(main_1_out_16));
  CONVERSOR_main main_2 (
    ._1(_1_2), ._2(_2_2), ._3(_3_2), ._4(_4_2), ._5(_5_2), ._6(_6_2), ._7(_7_2), ._8(_8_2), ._9(_9_2),
    .A(A_2), .B(B_2), .C(C_2), .D(D_2), .E(E_2), .F(F_2), .out_16(main_2_out_16));
  meiosomador_main main_3 (.A(main_2_out_16[0]), .B(main_1_out_16[0]), .S(main_3_s[0]), .VAI_1(main_3_vai_1));
  somadorinteiro_main main_4 (
    .VEM_1(main_5_vai_1), .A(main_2_out_16[3]), .B(main_1_out_16[3]), .S(main_3_s[3]), .vai_1(main_4_vai_1[0]));
  somadorinteiro_main main_5 (
    .VEM_1(main_6_vai_1), .A(main_1_out_16[2]), .B(main_2_out_16[2]), .S(main_3_s[2]), .vai_1(main_5_vai_1));
  somadorinteiro_main main_6 (
    .VEM_1(main_3_vai_1), .A(main_1_out_16[1]), .B(main_2_out_16[1]), .S(main_3_s[1]), .vai_1(main_6_vai_1));
  Hex_Digit_Display hex_digit_display_1 (.value({{3{in_17}}, main_4_vai_1[0]}));  // open: dp
  Hex_Digit_Display hex_digit_display_2 (.value(main_3_s));  // open: dp
endmodule
